// Digital circuit 2bit-multiplier.dig as structural Verilog
module _2bit_multiplier (
  input  a1,
  input  a0,
  input  b1,
  input  b0,
  output out_5,
  output out_6,
  output out_7,
  output out_8
);

  wire and_2_out, and_3_out, and_5_out, and_6_out, and_7_out, and_8_out;

  and and_1 (out_5, a1, a0, b1, b0);
  and and_2 (and_2_out, a1, ~a0, b1);  // And
  and and_3 (and_3_out, a1, b1, ~b0);  // And
  or or_1 (out_6, and_2_out, and_3_out);
  and and_4 (out_8, b0, a0);
  or or_2 (out_7, and_8_out, and_7_out, and_6_out, and_5_out);
  and and_5 (and_5_out, b1, a0, ~a1);  // And
  and and_6 (and_6_out, b0, ~b1, a1);  // And
  and and_7 (and_7_out, ~b0, b1, a0);  // And
  and and_8 (and_8_out, b0, ~a0, a1);  // And
endmodule
