// Digital circuit 4bit-adder.dig as structural Verilog
module _4bit_adder (
  input  Int_1,
  input  in_2,
  input  in_3,
  input  in_4,
  input  int_2,
  input  in_6,
  input  in_7,
  input  in_8,
  output Sum,
  output out_10,
  output out_11,
  output out_12,
  output cout
);

  wire and_1_out, and_2_out, and_3_out, and_4_out, and_5_out, and_6_out, and_7_out, and_8_out, and_9_out,
       and_10_out, and_11_out, and_12_out, and_13_out, and_14_out, and_15_out, and_16_out, and_17_out,
       and_18_out, and_19_out, and_20_out, and_21_out, and_22_out, or_3_out, or_5_out;

  or or_1 (out_12, Int_1, int_2);
  and and_1 (and_1_out, Int_1, int_2);
  and and_2 (and_2_out, ~in_2, ~in_6, and_1_out);  // And
  and and_3 (and_3_out, ~in_2, in_6, ~and_1_out);  // And
  and and_4 (and_4_out, in_2, ~in_6, ~and_1_out);  // And
  and and_5 (and_5_out, in_2, in_6, and_1_out);
  or or_2 (out_11, and_2_out, and_3_out, and_4_out, and_5_out);
  and and_6 (and_6_out, ~in_2, in_6, and_1_out);  // And
  and and_7 (and_7_out, in_2, ~in_6, and_1_out);  // And
  and and_8 (and_8_out, in_2, in_6, ~and_1_out);  // And
  or or_3 (or_3_out, and_6_out, and_7_out, and_8_out, and_5_out);
  and and_9 (and_9_out, ~in_3, ~in_7, or_3_out);  // And
  and and_10 (and_10_out, ~in_3, in_7, ~or_3_out);  // And
  and and_11 (and_11_out, in_3, ~in_7, ~or_3_out);  // And
  and and_12 (and_12_out, in_3, in_7, or_3_out);
  or or_4 (out_10, and_9_out, and_10_out, and_11_out, and_12_out);
  and and_13 (and_13_out, ~in_3, in_7, or_3_out);  // And
  and and_14 (and_14_out, in_3, ~in_7, or_3_out);  // And
  and and_15 (and_15_out, in_3, in_7, ~or_3_out);  // And
  or or_5 (or_5_out, and_13_out, and_14_out, and_15_out, and_12_out);
  and and_16 (and_16_out, ~in_4, ~in_8, or_5_out);  // And
  and and_17 (and_17_out, ~in_4, in_8, ~or_5_out);  // And
  and and_18 (and_18_out, in_4, ~in_8, ~or_5_out);  // And
  and and_19 (and_19_out, in_4, in_8, or_5_out);
  or or_6 (Sum, and_16_out, and_17_out, and_18_out, and_19_out);
  and and_20 (and_20_out, ~in_4, in_8, or_5_out);  // And
  and and_21 (and_21_out, in_4, ~in_8, or_5_out);  // And
  and and_22 (and_22_out, in_4, in_8, ~or_5_out);  // And
  or or_7 (cout, and_20_out, and_21_out, and_22_out, and_19_out);

  // Notes on the sheet:
  //   Top is lowest value
  //   Little Edian output
endmodule
