// Digital circuit counter.dig as structural Verilog
module counter (
  input  clk,
  input  dir,
  output out_3,
  output out_4
);

  wire and_1_out, and_2_out, and_3_out, and_4_out, not_1_out, or_1_out;

  not not_1 (not_1_out, out_4);
  D_FF d1 (.D(not_1_out), .C(clk), .Q(out_4));  // open: nQ
  D_FF d0 (.D(or_1_out), .C(clk), .Q(out_3));  // open: nQ
  and and_1 (and_1_out, ~dir, ~out_4, ~out_3);  // And
  and and_2 (and_2_out, dir, out_4, ~out_3);  // And
  and and_3 (and_3_out, ~dir, out_4, out_3);  // And
  and and_4 (and_4_out, dir, ~out_4, out_3);  // And
  or or_1 (or_1_out, and_1_out, and_2_out, and_3_out, and_4_out);
endmodule
